// Logisim project new  path.circ as structural Verilog: 2 circuits, main circuit main
module main (
  input  [4:0] in_1,
  input  [31:0] in_2,
  input  [31:0] in_3,
  output out_4,
  output [31:0] out_5
);

  wire comparator_1_lt, comparator_2_lt, comparator_3_eq, comparator_4_eq, comparator_4_gt, comparator_4_lt,
       comparator_5_eq, comparator_6_eq, not_1_out, or_2_out;
  wire [31:0] adder_1_out, and_1_out, multiplexer_1_out, multiplexer_2_out, multiplexer_3_out,
       multiplexer_4_out, multiplexer_5_out, multiplexer_6_out, or_1_out, shifter_1_out, shifter_2_out,
       shifter_3_out, subtractor_1_out, xor_1_out;

  assign and_1_out = in_2 & in_3;  // AND_Gate and_1, 32 bits wide
  assign or_1_out = in_2 | in_3;  // OR_Gate or_1, 32 bits wide
  Adder #(.width(32)) adder_1 (.a(in_2), .b(in_3), .out(adder_1_out));  // open: cin, cout
  Comparator #(.width(32), .mode("unsigned")) comparator_1 (.a(in_2), .b(in_3), .lt(comparator_1_lt));  // open: gt, eq
  Subtractor #(.width(32)) subtractor_1 (.a(in_2), .b(in_3), .out(subtractor_1_out));  // open: bin, bout
  Shifter #(.width(32), .shift("lr")) shifter_1 (.in(in_2), .\dist (in_3[4:0]), .out(shifter_1_out));
  Shifter #(.width(32), .shift("ar")) shifter_2 (.in(in_2), .\dist (in_3[4:0]), .out(shifter_2_out));
  Shifter #(.width(32)) shifter_3 (.in(in_2), .\dist (in_3[4:0]), .out(shifter_3_out));
  assign xor_1_out = in_2 ^ in_3;  // XOR_Gate xor_1, 32 bits wide
  Comparator #(.width(32)) comparator_2 (.a(in_2), .b(in_3), .lt(comparator_2_lt));  // open: gt, eq
  Comparator #(.width(32)) comparator_3 (.a(in_2), .b(in_3), .eq(comparator_3_eq));  // open: gt, lt
  Comparator #(.width(32)) comparator_4 (
    .a(in_2), .b(in_3), .gt(comparator_4_gt), .eq(comparator_4_eq), .lt(comparator_4_lt));
  Multiplexer #(.width(32), .disabled(0), .enable("false")) multiplexer_1 (
    .in0({32{1'b0}}), .in1(32'h1), .out(multiplexer_1_out), .sel(comparator_1_lt));
  or or_2 (or_2_out, comparator_4_gt, comparator_4_eq);
  Multiplexer #(.width(32), .disabled(0), .enable("false")) multiplexer_2 (
    .in0({32{1'b0}}), .in1(32'h1), .out(multiplexer_2_out), .sel(comparator_2_lt));
  Multiplexer #(.width(32), .disabled(0), .enable("false")) multiplexer_3 (
    .in0({32{1'b0}}), .in1(32'h1), .out(multiplexer_3_out), .sel(comparator_3_eq));
  Multiplexer #(.width(32), .disabled(0), .enable("false")) multiplexer_4 (
    .in0({32{1'b0}}), .in1(32'h1), .out(multiplexer_4_out), .sel(or_2_out));
  Multiplexer #(.width(32), .disabled(0), .enable("false")) multiplexer_5 (
    .in0({32{1'b0}}), .in1(32'h1), .out(multiplexer_5_out), .sel(comparator_4_lt));
  Multiplexer #(.width(32), .disabled(0), .enable("false")) multiplexer_6 (
    .in0({32{1'b0}}), .in1(32'h1), .out(multiplexer_6_out), .sel(not_1_out));
  not not_1 (not_1_out, comparator_4_eq);
  Multiplexer #(.select(5), .width(32), .disabled(0), .enable("false")) multiplexer_7 (
    .in0(adder_1_out), .in1(shifter_3_out), .in2(multiplexer_2_out), .in3(multiplexer_1_out),
    .in4(xor_1_out), .in5(shifter_1_out), .in6(or_1_out), .in7(and_1_out), .in8(subtractor_1_out),
    .in13(shifter_2_out), .in16(multiplexer_3_out), .in17(multiplexer_6_out), .in20(multiplexer_5_out),
    .in21(multiplexer_4_out), .out(out_5), .sel(in_1));  // open: in9, in10, in11, in12, in14, in15, in18, in19, in22, in23, in24, in25, in26, in27, in28, in29, in30, in31
  Comparator #(.width(2)) comparator_5 (.a(in_1[4:3]), .b(2'b10), .eq(comparator_5_eq));  // open: gt, lt
  Comparator #(.width(32)) comparator_6 (.a(32'h1), .b(out_5), .eq(comparator_6_eq));  // open: gt, lt
  and and_2 (out_4, comparator_5_eq, comparator_6_eq);

  // Notes on the sheet:
  //   A
  //   B
  //   19B-085-CS Muhammad Ashar
  //   Branch
endmodule

module regF (
  input  [31:0] in_1,
  input  [4:0] RS1,
  input  Wen,
  input  [4:0] RD,
  input  [4:0] RS2,
  input  in_6,
  output [31:0] out_7,
  output [31:0] out_8
);

  wire clock_1_out, decoder_1_out0, decoder_1_out1, decoder_1_out2, decoder_1_out3, decoder_1_out4,
       decoder_1_out5, decoder_1_out6, decoder_1_out7, decoder_1_out8, decoder_1_out9, decoder_1_out10,
       decoder_1_out11, decoder_1_out12, decoder_1_out13, decoder_1_out14, decoder_1_out15, decoder_1_out16,
       decoder_1_out17, decoder_1_out18, decoder_1_out19, decoder_1_out20, decoder_1_out21, decoder_1_out22,
       decoder_1_out23, decoder_1_out24, decoder_1_out25, decoder_1_out26, decoder_1_out27, decoder_1_out28,
       decoder_1_out29, decoder_1_out30, decoder_1_out31;
  wire [31:0] register_1_q, register_2_q, register_3_q, register_4_q, register_5_q, register_6_q,
       register_7_q, register_8_q, register_9_q, register_10_q, register_11_q, register_12_q, register_13_q,
       register_14_q, register_15_q, register_16_q, register_17_q, register_18_q, register_19_q,
       register_20_q, register_21_q, register_22_q, register_23_q, register_24_q, register_25_q,
       register_26_q, register_27_q, register_28_q, register_29_q, register_30_q, register_31_q,
       register_32_q;

  Decoder #(.select(5)) decoder_1 (
    .out0(decoder_1_out0), .out1(decoder_1_out1), .out2(decoder_1_out2), .out3(decoder_1_out3),
    .out4(decoder_1_out4), .out5(decoder_1_out5), .out6(decoder_1_out6), .out7(decoder_1_out7),
    .out8(decoder_1_out8), .out9(decoder_1_out9), .out10(decoder_1_out10), .out11(decoder_1_out11),
    .out12(decoder_1_out12), .out13(decoder_1_out13), .out14(decoder_1_out14), .out15(decoder_1_out15),
    .out16(decoder_1_out16), .out17(decoder_1_out17), .out18(decoder_1_out18), .out19(decoder_1_out19),
    .out20(decoder_1_out20), .out21(decoder_1_out21), .out22(decoder_1_out22), .out23(decoder_1_out23),
    .out24(decoder_1_out24), .out25(decoder_1_out25), .out26(decoder_1_out26), .out27(decoder_1_out27),
    .out28(decoder_1_out28), .out29(decoder_1_out29), .out30(decoder_1_out30), .out31(decoder_1_out31),
    .sel(RD), .en(Wen));
  Clock clock_1 (.out(clock_1_out));
  Register #(.width(32)) register_1 (
    .D({32{1'b0}}), .en(decoder_1_out0), .Q(register_1_q), .clk(clock_1_out), .clr(in_6));
  Register #(.width(32)) register_2 (.D(in_1), .en(decoder_1_out1), .Q(register_2_q), .clk(clock_1_out), .clr(in_6));
  Register #(.width(32)) register_3 (.D(in_1), .en(decoder_1_out2), .Q(register_3_q), .clk(clock_1_out), .clr(in_6));
  Register #(.width(32)) register_4 (.D(in_1), .en(decoder_1_out3), .Q(register_4_q), .clk(clock_1_out), .clr(in_6));
  Register #(.width(32)) register_5 (.D(in_1), .en(decoder_1_out4), .Q(register_5_q), .clk(clock_1_out), .clr(in_6));
  Register #(.width(32)) register_6 (.D(in_1), .en(decoder_1_out5), .Q(register_6_q), .clk(clock_1_out), .clr(in_6));
  Register #(.width(32)) register_7 (.D(in_1), .en(decoder_1_out6), .Q(register_7_q), .clk(clock_1_out), .clr(in_6));
  Register #(.width(32)) register_8 (.D(in_1), .en(decoder_1_out7), .Q(register_8_q), .clk(clock_1_out), .clr(in_6));
  Register #(.width(32)) register_9 (.D(in_1), .en(decoder_1_out8), .Q(register_9_q), .clk(clock_1_out), .clr(in_6));
  Register #(.width(32)) register_10 (.D(in_1), .en(decoder_1_out9), .Q(register_10_q), .clk(clock_1_out), .clr(in_6));
  Register #(.width(32)) register_11 (.D(in_1), .en(decoder_1_out10), .Q(register_11_q), .clk(clock_1_out), .clr(in_6));
  Register #(.width(32)) register_12 (.D(in_1), .en(decoder_1_out11), .Q(register_12_q), .clk(clock_1_out), .clr(in_6));
  Register #(.width(32)) register_13 (.D(in_1), .en(decoder_1_out12), .Q(register_13_q), .clk(clock_1_out), .clr(in_6));
  Register #(.width(32)) register_14 (.D(in_1), .en(decoder_1_out13), .Q(register_14_q), .clk(clock_1_out), .clr(in_6));
  Register #(.width(32)) register_15 (.D(in_1), .en(decoder_1_out14), .Q(register_15_q), .clk(clock_1_out), .clr(in_6));
  Register #(.width(32)) register_16 (.D(in_1), .en(decoder_1_out15), .Q(register_16_q), .clk(clock_1_out), .clr(in_6));
  Register #(.width(32)) register_17 (.D(in_1), .en(decoder_1_out16), .Q(register_17_q), .clk(clock_1_out), .clr(in_6));
  Register #(.width(32)) register_18 (.D(in_1), .en(decoder_1_out17), .Q(register_18_q), .clk(clock_1_out), .clr(in_6));
  Register #(.width(32)) register_19 (.D(in_1), .en(decoder_1_out18), .Q(register_19_q), .clk(clock_1_out), .clr(in_6));
  Register #(.width(32)) register_20 (.D(in_1), .en(decoder_1_out19), .Q(register_20_q), .clk(clock_1_out), .clr(in_6));
  Register #(.width(32)) register_21 (.D(in_1), .en(decoder_1_out20), .Q(register_21_q), .clk(clock_1_out), .clr(in_6));
  Register #(.width(32)) register_22 (.D(in_1), .en(decoder_1_out21), .Q(register_22_q), .clk(clock_1_out), .clr(in_6));
  Register #(.width(32)) register_23 (.D(in_1), .en(decoder_1_out22), .Q(register_23_q), .clk(clock_1_out), .clr(in_6));
  Register #(.width(32)) register_24 (.D(in_1), .en(decoder_1_out23), .Q(register_24_q), .clk(clock_1_out), .clr(in_6));
  Register #(.width(32)) register_25 (.D(in_1), .en(decoder_1_out24), .Q(register_25_q), .clk(clock_1_out), .clr(in_6));
  Register #(.width(32)) register_26 (.D(in_1), .en(decoder_1_out25), .Q(register_26_q), .clk(clock_1_out), .clr(in_6));
  Register #(.width(32)) register_27 (.D(in_1), .en(decoder_1_out26), .Q(register_27_q), .clk(clock_1_out), .clr(in_6));
  Register #(.width(32)) register_28 (.D(in_1), .en(decoder_1_out27), .Q(register_28_q), .clk(clock_1_out), .clr(in_6));
  Register #(.width(32)) register_29 (.D(in_1), .en(decoder_1_out28), .Q(register_29_q), .clk(clock_1_out), .clr(in_6));
  Register #(.width(32)) register_30 (.D(in_1), .en(decoder_1_out29), .Q(register_30_q), .clk(clock_1_out), .clr(in_6));
  Register #(.width(32)) register_31 (.D(in_1), .en(decoder_1_out30), .Q(register_31_q), .clk(clock_1_out), .clr(in_6));
  Register #(.width(32)) register_32 (.D(in_1), .en(decoder_1_out31), .Q(register_32_q), .clk(clock_1_out), .clr(in_6));
  Multiplexer #(.select(5), .width(32), .enable("false")) multiplexer_1 (
    .in0(register_1_q), .in1(register_2_q), .in2(register_3_q), .in3(register_4_q), .in4(register_5_q),
    .in5(register_6_q), .in6(register_7_q), .in7(register_8_q), .in8(register_9_q), .in9(register_10_q),
    .in10(register_11_q), .in11(register_12_q), .in12(register_13_q), .in13(register_14_q),
    .in14(register_15_q), .in15(register_16_q), .in16(register_17_q), .in17(register_18_q),
    .in18(register_19_q), .in19(register_20_q), .in20(register_21_q), .in21(register_22_q),
    .in22(register_23_q), .in23(register_24_q), .in24(register_25_q), .in25(register_26_q),
    .in26(register_27_q), .in27(register_28_q), .in28(register_29_q), .in29(register_30_q),
    .in30(register_31_q), .in31(register_32_q), .out(out_7), .sel(RS1));
  Multiplexer #(.select(5), .width(32), .enable("false")) multiplexer_2 (
    .in0(register_1_q), .in1(register_2_q), .in2(register_3_q), .in3(register_4_q), .in4(register_5_q),
    .in5(register_6_q), .in6(register_7_q), .in7(register_8_q), .in8(register_9_q), .in9(register_10_q),
    .in10(register_11_q), .in11(register_12_q), .in12(register_13_q), .in13(register_14_q),
    .in14(register_15_q), .in15(register_16_q), .in16(register_17_q), .in17(register_18_q),
    .in18(register_19_q), .in19(register_20_q), .in20(register_21_q), .in21(register_22_q),
    .in22(register_23_q), .in23(register_24_q), .in24(register_25_q), .in25(register_26_q),
    .in26(register_27_q), .in27(register_28_q), .in28(register_29_q), .in29(register_30_q),
    .in30(register_31_q), .in31(register_32_q), .out(out_8), .sel(RS2));
endmodule
